// Logisim project myCPU.circ as structural Verilog: 12 circuits, main circuit main
module main (
  input  Prescaler
);

  wire c_t, cu_1_alu_enable, cu_1_ddrenable, cu_1_mask, cu_1_pcenable, cu_1_pin_enable, cu_1_port_enable,
       cu_1_prescaler1, cu_1_prescaler2, cu_1_ramwrtieenable, cu_1_reg1enable, cu_1_reg2enable,
       cu_1_reg3enable, cu_1_reg4enable, cu_1_reg5enable, cu_1_spenable, cu_1_update,
       tram_controller_1_enable, tram_controller_1_out_11;
  wire [0:0] binary_to_bcd_converter_4_p1;
  wire [3:0] mydecoder_1_operand1, mydecoder_1_operand2;
  wire [7:0] A, alu_1_result, B, binary_to_bcd_converter_1_p1, binary_to_bcd_converter_2_p1,
       binary_to_bcd_converter_5_p1, binary_to_bcd_converter_7_p1, C, cu_1_alu_select, cu_1_aluinput1,
       cu_1_aluinput2, cu_1_ramadress, cu_1_raminput, D, E, mydecoder_1_data1, mydecoder_1_data2,
       mydecoder_1_instruction, pc, pcData, port_controller_1_out_8, port_controller_1_out_9,
       port_controller_1_out_11, regData, register_1_q, RRAM_dout, RV_q, sp, tram_controller_1_out_12,
       tram_controller_1_prescalero;
  wire [31:0] rom_1_data;

  _7_Segment_Display u_7_segment_display_1 ();  // open: g, f, a, b, e, d, c, dp
  // BCD_to_7_Segment_decoder bcd_to_7_segment_decoder_1: pin names not known
  // Binary_to_BCD_converter #(.binvalue(8)) binary_to_bcd_converter_1: pin names not known; wires that end beside it: binary_to_bcd_converter_1_p1
  _7_Segment_Display u_7_segment_display_2 ();  // open: g, f, a, b, e, d, c, dp
  // BCD_to_7_Segment_decoder bcd_to_7_segment_decoder_2: pin names not known
  // Binary_to_BCD_converter #(.binvalue(8)) binary_to_bcd_converter_2: pin names not known; wires that end beside it: binary_to_bcd_converter_2_p1
  _7_Segment_Display u_7_segment_display_3 ();  // open: g, f, a, b, e, d, c, dp
  // BCD_to_7_Segment_decoder bcd_to_7_segment_decoder_3: pin names not known
  // Binary_to_BCD_converter #(.binvalue(8)) binary_to_bcd_converter_3: pin names not known; wires that end beside it: pc
  _7_Segment_Display u_7_segment_display_4 ();  // open: g, f, a, b, e, d, c, dp
  _7_Segment_Display u_7_segment_display_5 ();  // open: g, f, a, b, e, d, c, dp
  // BCD_to_7_Segment_decoder bcd_to_7_segment_decoder_4: pin names not known
  // BCD_to_7_Segment_decoder bcd_to_7_segment_decoder_5: pin names not known
  _7_Segment_Display u_7_segment_display_6 ();  // open: g, f, a, b, e, d, c, dp
  _7_Segment_Display u_7_segment_display_7 ();  // open: g, f, a, b, e, d, c, dp
  // BCD_to_7_Segment_decoder bcd_to_7_segment_decoder_6: pin names not known
  // BCD_to_7_Segment_decoder bcd_to_7_segment_decoder_7: pin names not known
  Clock clock_1 (.out(c_t));
  _7_Segment_Display u_7_segment_display_8 ();  // open: g, f, a, b, e, d, c, dp
  _7_Segment_Display u_7_segment_display_9 ();  // open: g, f, a, b, e, d, c, dp
  // BCD_to_7_Segment_decoder bcd_to_7_segment_decoder_8: pin names not known
  // BCD_to_7_Segment_decoder bcd_to_7_segment_decoder_9: pin names not known; wires that end beside it: Prescaler
  _7_Segment_Display u_7_segment_display_10 ();  // open: g, f, a, b, e, d, c, dp
  // BCD_to_7_Segment_decoder bcd_to_7_segment_decoder_10: pin names not known
  // Binary_to_BCD_converter #(.binvalue(4)) binary_to_bcd_converter_4: pin names not known; wires that end beside it: {3'b000, binary_to_bcd_converter_4_p1[0]}
  _7_Segment_Display u_7_segment_display_11 ();  // open: g, f, a, b, e, d, c, dp
  // BCD_to_7_Segment_decoder bcd_to_7_segment_decoder_11: pin names not known
  _7_Segment_Display u_7_segment_display_12 ();  // open: g, f, a, b, e, d, c, dp
  // BCD_to_7_Segment_decoder bcd_to_7_segment_decoder_12: pin names not known
  _7_Segment_Display u_7_segment_display_13 ();  // open: g, f, a, b, e, d, c, dp
  // BCD_to_7_Segment_decoder bcd_to_7_segment_decoder_13: pin names not known
  // Binary_to_BCD_converter #(.binvalue(8)) binary_to_bcd_converter_5: pin names not known; wires that end beside it: binary_to_bcd_converter_5_p1
  ROM #(.dataWidth(32)) rom_1 (.addr(pc), .data(rom_1_data));
  PCcontrol pccontrol_1 (
    .romAdress(pc), .c(c_t), .presc(8'h3), .in_5(tram_controller_1_out_11), .pcE(tram_controller_1_enable),
    .pcI(pcData));
  TRAM_CONTROLLER tram_controller_1 (
    .out_10(binary_to_bcd_converter_4_p1[0]), .pcData(pcData), .prescalerO(tram_controller_1_prescalero),
    .Enable(tram_controller_1_enable), .out_12(tram_controller_1_out_12), .out_11(tram_controller_1_out_11),
    .maskEnable(cu_1_mask), .c(c_t), .prescEnable(cu_1_prescaler1), .mask(regData), .prescaler(regData),
    .regData(regData), .pcEnable(cu_1_pcenable));
  _7_Segment_Display u_7_segment_display_14 ();  // open: g, f, a, b, e, d, c, dp
  _7_Segment_Display u_7_segment_display_15 ();  // open: g, f, a, b, e, d, c, dp
  // BCD_to_7_Segment_decoder bcd_to_7_segment_decoder_14: pin names not known
  // BCD_to_7_Segment_decoder bcd_to_7_segment_decoder_15: pin names not known
  // Binary_to_BCD_converter #(.binvalue(8)) binary_to_bcd_converter_6: pin names not known; wires that end beside it: tram_controller_1_out_12
  _7_Segment_Display u_7_segment_display_16 ();  // open: g, f, a, b, e, d, c, dp
  // BCD_to_7_Segment_decoder bcd_to_7_segment_decoder_16: pin names not known
  _7_Segment_Display u_7_segment_display_17 ();  // open: g, f, a, b, e, d, c, dp
  // BCD_to_7_Segment_decoder bcd_to_7_segment_decoder_17: pin names not known
  _7_Segment_Display u_7_segment_display_18 ();  // open: g, f, a, b, e, d, c, dp
  // BCD_to_7_Segment_decoder bcd_to_7_segment_decoder_18: pin names not known
  // Binary_to_BCD_converter #(.binvalue(8)) binary_to_bcd_converter_7: pin names not known; wires that end beside it: binary_to_bcd_converter_7_p1
  PORT_CONTROLLER port_controller_1 (
    .Ooutput(binary_to_bcd_converter_7_p1), .out_12(binary_to_bcd_converter_5_p1),
    .out_11(port_controller_1_out_11), .Counter(binary_to_bcd_converter_1_p1),
    .out_8(port_controller_1_out_8), .out_14(binary_to_bcd_converter_2_p1), .out_9(port_controller_1_out_9),
    .PrescalerEnable(cu_1_prescaler2), .DDREnable(cu_1_ddrenable), .RegData(regData), .clk(c_t),
    .portEnable(cu_1_port_enable), .UpdateEnable(cu_1_update), .InputEnable(cu_1_pin_enable));
  _7_Segment_Display u_7_segment_display_19 ();  // open: g, f, a, b, e, d, c, dp
  // BCD_to_7_Segment_decoder bcd_to_7_segment_decoder_19: pin names not known
  // Binary_to_BCD_converter #(.binvalue(8)) binary_to_bcd_converter_8: pin names not known; wires that end beside it: tram_controller_1_prescalero
  _7_Segment_Display u_7_segment_display_20 ();  // open: g, f, a, b, e, d, c, dp
  _7_Segment_Display u_7_segment_display_21 ();  // open: g, f, a, b, e, d, c, dp
  // BCD_to_7_Segment_decoder bcd_to_7_segment_decoder_20: pin names not known
  // BCD_to_7_Segment_decoder bcd_to_7_segment_decoder_21: pin names not known
  _7_Segment_Display u_7_segment_display_22 ();  // open: g, f, a, b, e, d, c, dp
  // BCD_to_7_Segment_decoder bcd_to_7_segment_decoder_22: pin names not known
  _7_Segment_Display u_7_segment_display_23 ();  // open: g, f, a, b, e, d, c, dp
  // BCD_to_7_Segment_decoder bcd_to_7_segment_decoder_23: pin names not known
  // Binary_to_BCD_converter #(.binvalue(8)) binary_to_bcd_converter_9: pin names not known; wires that end beside it: port_controller_1_out_8
  myDecoder mydecoder_1 (
    .instruction(mydecoder_1_instruction), .operand1(mydecoder_1_operand1), .data1(mydecoder_1_data1),
    .operand2(mydecoder_1_operand2), .data2(mydecoder_1_data2), .command(rom_1_data));
  _7_Segment_Display u_7_segment_display_24 ();  // open: g, f, a, b, e, d, c, dp
  // BCD_to_7_Segment_decoder bcd_to_7_segment_decoder_24: pin names not known
  _7_Segment_Display u_7_segment_display_25 ();  // open: g, f, a, b, e, d, c, dp
  // BCD_to_7_Segment_decoder bcd_to_7_segment_decoder_25: pin names not known
  _7_Segment_Display u_7_segment_display_26 ();  // open: g, f, a, b, e, d, c, dp
  // BCD_to_7_Segment_decoder bcd_to_7_segment_decoder_26: pin names not known
  _7_Segment_Display u_7_segment_display_27 ();  // open: g, f, a, b, e, d, c, dp
  _7_Segment_Display u_7_segment_display_28 ();  // open: g, f, a, b, e, d, c, dp
  // BCD_to_7_Segment_decoder bcd_to_7_segment_decoder_27: pin names not known
  // BCD_to_7_Segment_decoder bcd_to_7_segment_decoder_28: pin names not known
  // Binary_to_BCD_converter #(.binvalue(8)) binary_to_bcd_converter_10: pin names not known; wires that end beside it: port_controller_1_out_9
  CU cu_1 (
    .regData(regData), .ramInput(cu_1_raminput), .ramAdress(cu_1_ramadress),
    .ramWrtieEnable(cu_1_ramwrtieenable), .ALU_select(cu_1_alu_select), .ALU_enable(cu_1_alu_enable),
    .ALUinput1(cu_1_aluinput1), .ALUinput2(cu_1_aluinput2), .reg1Enable(cu_1_reg1enable),
    .reg2Enable(cu_1_reg2enable), .reg3Enable(cu_1_reg3enable), .reg5Enable(cu_1_reg5enable),
    .reg4Enable(cu_1_reg4enable), .SPEnable(cu_1_spenable), .PCEnable(cu_1_pcenable),
    .ddrEnable(cu_1_ddrenable), .PORT_Enable(cu_1_port_enable), .PIN_Enable(cu_1_pin_enable),
    .update(cu_1_update), .prescaler2(cu_1_prescaler2), .prescaler1(cu_1_prescaler1), .mask(cu_1_mask),
    .RegB(B), .clock(c_t), .ramOutput(RRAM_dout), .RegC(C), .operand1(mydecoder_1_operand1),
    .operand2(mydecoder_1_operand2), .data1(mydecoder_1_data1), .data2(mydecoder_1_data2), .RegD(D),
    .insturction(mydecoder_1_instruction), .RegE(E), .RV(RV_q), .SP(sp), .PC(pc),
    .DDR(port_controller_1_out_8), .POoRT(port_controller_1_out_9), .Iinput(port_controller_1_out_11),
    .maskNotifier(tram_controller_1_out_11), .RegA(A));  // open: ramoutputEnable, RVEnable
  Register u_SP (.D(regData), .en(cu_1_spenable), .clk(c_t), .Q(sp));  // open: clr
  _7_Segment_Display u_7_segment_display_29 ();  // open: g, f, a, b, e, d, c, dp
  // BCD_to_7_Segment_decoder bcd_to_7_segment_decoder_29: pin names not known
  Register RegA (.D(regData), .en(cu_1_reg1enable), .clk(c_t), .Q(A));  // open: clr
  RAM RRAM (
    .addr(cu_1_ramadress), .we(cu_1_ramwrtieenable), .oe(1'b1), .clk(c_t), .din(cu_1_raminput),
    .dout(RRAM_dout));
  Register RegB (.D(regData), .en(cu_1_reg2enable), .clk(c_t), .Q(B));  // open: clr
  Register RegC (.D(regData), .en(cu_1_reg3enable), .clk(c_t), .Q(C));  // open: clr
  Register RegD (.D(regData), .en(cu_1_reg4enable), .clk(c_t), .Q(D));  // open: clr
  Register RV (.D(alu_1_result), .en(cu_1_alu_enable), .clk(c_t), .Q(RV_q));  // open: clr
  ALU alu_1 (
    .result(alu_1_result), .Enable(cu_1_alu_enable), .selct(cu_1_alu_select), .input1(cu_1_aluinput1),
    .input2(cu_1_aluinput2));
  Register register_1 (.D(RRAM_dout), .en(cu_1_ramwrtieenable), .clk(c_t), .Q(register_1_q));  // open: clr
  Register RegE (.D(regData), .en(cu_1_reg5enable), .clk(c_t), .Q(E));  // open: clr
  _7_Segment_Display u_7_segment_display_30 ();  // open: g, f, a, b, e, d, c, dp
  // BCD_to_7_Segment_decoder bcd_to_7_segment_decoder_30: pin names not known
  _7_Segment_Display u_7_segment_display_31 ();  // open: g, f, a, b, e, d, c, dp
  // BCD_to_7_Segment_decoder bcd_to_7_segment_decoder_31: pin names not known
  // Buzzer #(.vol_width(2)) buzzer_1: pin names not known; wires that end beside it: 14'h800, cu_1_ramwrtieenable, 2'b11
  _7_Segment_Display u_7_segment_display_32 ();  // open: g, f, a, b, e, d, c, dp
  // BCD_to_7_Segment_decoder bcd_to_7_segment_decoder_32: pin names not known
  _7_Segment_Display u_7_segment_display_33 ();  // open: g, f, a, b, e, d, c, dp
  // BCD_to_7_Segment_decoder bcd_to_7_segment_decoder_33: pin names not known
  // Binary_to_BCD_converter #(.binvalue(8)) binary_to_bcd_converter_11: pin names not known; wires that end beside it: RV_q
  _7_Segment_Display u_7_segment_display_34 ();  // open: g, f, a, b, e, d, c, dp
  // BCD_to_7_Segment_decoder bcd_to_7_segment_decoder_34: pin names not known
  // Binary_to_BCD_converter #(.binvalue(8)) binary_to_bcd_converter_12: pin names not known; wires that end beside it: register_1_q
  _7_Segment_Display u_7_segment_display_35 ();  // open: g, f, a, b, e, d, c, dp
  // BCD_to_7_Segment_decoder bcd_to_7_segment_decoder_35: pin names not known
  // Binary_to_BCD_converter #(.binvalue(8)) binary_to_bcd_converter_13: pin names not known; wires that end beside it: sp
  _7_Segment_Display u_7_segment_display_36 ();  // open: g, f, a, b, e, d, c, dp
  // BCD_to_7_Segment_decoder bcd_to_7_segment_decoder_36: pin names not known
  _7_Segment_Display u_7_segment_display_37 ();  // open: g, f, a, b, e, d, c, dp
  // BCD_to_7_Segment_decoder bcd_to_7_segment_decoder_37: pin names not known
  _7_Segment_Display u_7_segment_display_38 ();  // open: g, f, a, b, e, d, c, dp
  // BCD_to_7_Segment_decoder bcd_to_7_segment_decoder_38: pin names not known
  _7_Segment_Display u_7_segment_display_39 ();  // open: g, f, a, b, e, d, c, dp
  // BCD_to_7_Segment_decoder bcd_to_7_segment_decoder_39: pin names not known
  // Binary_to_BCD_converter #(.binvalue(8)) binary_to_bcd_converter_14: pin names not known; wires that end beside it: A
  _7_Segment_Display u_7_segment_display_40 ();  // open: g, f, a, b, e, d, c, dp
  // BCD_to_7_Segment_decoder bcd_to_7_segment_decoder_40: pin names not known
  // Binary_to_BCD_converter #(.binvalue(8)) binary_to_bcd_converter_15: pin names not known; wires that end beside it: B
  _7_Segment_Display u_7_segment_display_41 ();  // open: g, f, a, b, e, d, c, dp
  // BCD_to_7_Segment_decoder bcd_to_7_segment_decoder_41: pin names not known
  // Binary_to_BCD_converter #(.binvalue(8)) binary_to_bcd_converter_16: pin names not known; wires that end beside it: C
  _7_Segment_Display u_7_segment_display_42 ();  // open: g, f, a, b, e, d, c, dp
  // BCD_to_7_Segment_decoder bcd_to_7_segment_decoder_42: pin names not known
  // Binary_to_BCD_converter #(.binvalue(8)) binary_to_bcd_converter_17: pin names not known; wires that end beside it: D
  _7_Segment_Display u_7_segment_display_43 ();  // open: g, f, a, b, e, d, c, dp
  // BCD_to_7_Segment_decoder bcd_to_7_segment_decoder_43: pin names not known
  // Binary_to_BCD_converter #(.binvalue(8)) binary_to_bcd_converter_18: pin names not known; wires that end beside it: E
  _7_Segment_Display u_7_segment_display_44 ();  // open: g, f, a, b, e, d, c, dp
  _7_Segment_Display u_7_segment_display_45 ();  // open: g, f, a, b, e, d, c, dp
  // BCD_to_7_Segment_decoder bcd_to_7_segment_decoder_44: pin names not known
  // BCD_to_7_Segment_decoder bcd_to_7_segment_decoder_45: pin names not known
  _7_Segment_Display u_7_segment_display_46 ();  // open: g, f, a, b, e, d, c, dp
  _7_Segment_Display u_7_segment_display_47 ();  // open: g, f, a, b, e, d, c, dp
  // BCD_to_7_Segment_decoder bcd_to_7_segment_decoder_46: pin names not known
  // BCD_to_7_Segment_decoder bcd_to_7_segment_decoder_47: pin names not known
  _7_Segment_Display u_7_segment_display_48 ();  // open: g, f, a, b, e, d, c, dp
  _7_Segment_Display u_7_segment_display_49 ();  // open: g, f, a, b, e, d, c, dp
  // BCD_to_7_Segment_decoder bcd_to_7_segment_decoder_48: pin names not known
  // BCD_to_7_Segment_decoder bcd_to_7_segment_decoder_49: pin names not known
  _7_Segment_Display u_7_segment_display_50 ();  // open: g, f, a, b, e, d, c, dp
  _7_Segment_Display u_7_segment_display_51 ();  // open: g, f, a, b, e, d, c, dp
  // BCD_to_7_Segment_decoder bcd_to_7_segment_decoder_50: pin names not known
  // BCD_to_7_Segment_decoder bcd_to_7_segment_decoder_51: pin names not known
  _7_Segment_Display u_7_segment_display_52 ();  // open: g, f, a, b, e, d, c, dp
  _7_Segment_Display u_7_segment_display_53 ();  // open: g, f, a, b, e, d, c, dp
  // BCD_to_7_Segment_decoder bcd_to_7_segment_decoder_52: pin names not known
  // BCD_to_7_Segment_decoder bcd_to_7_segment_decoder_53: pin names not known

  // Notes on the sheet:
  //   COUNTER
  //   PC
  //   MASK
  //   INPUT
  //   contents of rom_1 (hex, n*v repeats v):
  //   a003000 8100001 c019000 9100002 a105004 8104000 c00a000 8104001 c010000 a001007 3100002 a105000
  //   a100106 106001 a105006 a001007 2100003 a105000 100001 a105000 a100106 106001 a105006 a001007
  //   COUNTER
  //   ATVLA PIRIQIT IYO SADGACA
  //   OUTPUT
  //   Prescaler
  //   DDR
  //   PORT
  //   RV
  //   RAM
  //   SP
  //   A
  //   B
  //   C
  //   D
  //   E
endmodule

module ALU (
  input  [7:0] input1,
  input  [7:0] input2,
  input  [7:0] selct,
  input  Enable,
  output [7:0] result
);

  wire comparator_1_eq;
  wire [7:0] adder_1_out, and_1_out, bit_extender_1_out, divider_1_out, divider_1_rem, multiplier_1_out,
       not_1_out, or_1_out, subtractor_1_out, xor_1_out;

  Adder adder_1 (.a(input1), .b(input2), .out(adder_1_out));  // open: cin, cout
  Subtractor subtractor_1 (.a(input1), .b(input2), .out(subtractor_1_out));  // open: bin, bout
  Multiplier multiplier_1 (.a(input1), .b(input2), .out(multiplier_1_out));  // open: cin, cout
  Divider divider_1 (.a(input1), .b(input2), .out(divider_1_out), .rem(divider_1_rem));  // open: upper
  assign or_1_out = input1 | input2;  // OR_Gate or_1, 8 bits wide
  assign xor_1_out = input1 ^ input2;  // XOR_Gate xor_1, 8 bits wide
  assign and_1_out = input1 & input2;  // AND_Gate and_1, 8 bits wide
  assign not_1_out = ~input1;  // NOT_Gate not_1, 8 bits wide
  Comparator #(.mode("unsigned")) comparator_1 (.a(input1), .b(input2), .eq(comparator_1_eq));  // open: gt, lt
  assign bit_extender_1_out = {{7{comparator_1_eq}}, comparator_1_eq};  // Bit_Extender bit_extender_1
  Multiplexer #(.enable("true"), .select(4), .width(8)) multiplexer_1 (
    .in0(adder_1_out), .in1(subtractor_1_out), .in2(multiplier_1_out), .in3(divider_1_out), .in4(or_1_out),
    .in5(xor_1_out), .in6(and_1_out), .in7(not_1_out), .in8(bit_extender_1_out), .in9(divider_1_rem),
    .out(result), .sel(selct[3:0]), .en(Enable));  // open: in10, in11, in12, in13, in14, in15
endmodule

module CU (
  input  [7:0] insturction,
  input  [7:0] ramOutput,
  input  [3:0] operand1,
  input  [7:0] data1,
  input  [3:0] operand2,
  input  [7:0] data2,
  input  clock,
  input  [7:0] RegA,
  input  [7:0] RegB,
  input  [7:0] RegC,
  input  [7:0] RegD,
  input  [7:0] RegE,
  input  [7:0] SP,
  input  [7:0] PC,
  input  [7:0] DDR,
  input  [7:0] POoRT,
  input  [7:0] Iinput,
  input  [7:0] RV,
  input  maskNotifier,
  output ALU_enable,
  output [7:0] ALUinput1,
  output [7:0] ALUinput2,
  output [7:0] ALU_select,
  output [7:0] ramInput,
  output ramoutputEnable,
  output [7:0] ramAdress,
  output ramWrtieEnable,
  output [7:0] regData,
  output reg1Enable,
  output reg3Enable,
  output SPEnable,
  output ddrEnable,
  output PIN_Enable,
  output prescaler2,
  output mask,
  output reg2Enable,
  output reg4Enable,
  output RVEnable,
  output PORT_Enable,
  output update,
  output prescaler1,
  output PCEnable,
  output reg5Enable
);

  wire and_1_out, and_2_out, and_3_out, comparator_1_eq, comparator_2_eq, comparator_3_eq, comparator_4_eq,
       comparator_4_gt, comparator_5_eq, comparator_6_gt, comparator_7_gt, comparator_8_gt,
       demultiplexer_1_out4, demultiplexer_1_out7, not_1_out, or_3_out, or_4_out;
  wire [1:0] multiplexer_3_out, operand1_t, operand2_t;
  wire [2:0] bit_extender_4_out;
  wire [3:0] bit_extender_1_out, bit_extender_5_out;
  wire [7:0] multiplexer_1_out, multiplexer_7_out, selectedReg1, selectedReg2;

  Bit_Extender #(.out_width(4)) bit_extender_1 (.in(multiplexer_1_out), .out(bit_extender_1_out));
  Multiplexer #(.width(8)) multiplexer_1 (.in0(data1), .in1(8'h7), .out(multiplexer_1_out), .sel(maskNotifier));
  Bit_Extender #(.in_width(4), .out_width(2)) bit_extender_2 (.in(operand1), .out(operand1_t));
  Bit_Extender #(.in_width(4), .out_width(2)) bit_extender_3 (.in(operand2), .out(operand2_t));
  Comparator #(.mode("unsigned")) comparator_1 (
    .a(insturction), .b(8'ha), .eq(comparator_1_eq), .lt(ALU_enable));  // open: gt
  Multiplexer #(.select(4), .width(8)) multiplexer_2 (
    .in0(RegA), .in1(RegB), .in2(RegC), .in3(RegD), .in4(RegE), .in5(RV), .in6(SP), .in7(PC), .in8(DDR),
    .in9(POoRT), .in10(Iinput), .out(selectedReg1), .sel(bit_extender_1_out));  // open: in11, in12, in13, in14, in15
  Multiplexer #(.width(2)) multiplexer_3 (.in0(operand1_t), .in1(2'b01), .out(multiplexer_3_out), .sel(maskNotifier));
  Multiplexer #(.select(2), .width(8)) multiplexer_4 (
    .in0(data1), .in1(selectedReg1), .in2(ramOutput), .in3(ramOutput), .out(ALUinput1),
    .sel(multiplexer_3_out));
  Multiplexer #(.select(3), .width(8)) multiplexer_5 (
    .in0(RegA), .in1(RegB), .in2(RegC), .in3(RegD), .in4(RegE), .in5(RV), .in6(SP), .in7(PC),
    .out(selectedReg2), .sel(bit_extender_4_out));
  Bit_Extender #(.out_width(3)) bit_extender_4 (.in(data2), .out(bit_extender_4_out));
  Multiplexer #(.select(2), .width(8)) multiplexer_6 (
    .in0(data2), .in1(selectedReg2), .in2(data2), .out(ALUinput2), .sel(operand2_t));  // open: in3
  Comparator comparator_2 (.a({8{1'b1}}), .b(RV), .eq(comparator_2_eq));  // open: gt, lt
  Comparator comparator_3 (.a(RV), .b({8{1'b0}}), .eq(comparator_3_eq));  // open: gt, lt
  Comparator comparator_4 (.a(insturction), .b(8'hc), .gt(comparator_4_gt), .eq(comparator_4_eq));  // open: lt
  and and_1 (and_1_out, comparator_2_eq, comparator_4_eq);
  and and_2 (and_2_out, comparator_3_eq, comparator_4_gt);
  not not_1 (not_1_out, maskNotifier);
  Bit_Extender #(.out_width(4)) bit_extender_5 (.in(data2), .out(bit_extender_5_out));
  or or_1 (reg5Enable, maskNotifier, demultiplexer_1_out4);
  Comparator #(.mode("unsigned"), .width(2)) comparator_5 (
    .a(operand2_t), .b(2'b00), .eq(comparator_5_eq));  // open: gt, lt
  and and_3 (and_3_out, comparator_5_eq, not_1_out, comparator_1_eq);
  Demultiplexer #(.select(4)) demultiplexer_1 (
    .out0(reg1Enable), .out1(reg2Enable), .out2(reg3Enable), .out3(reg4Enable), .out4(demultiplexer_1_out4),
    .out5(RVEnable), .out6(SPEnable), .out7(demultiplexer_1_out7), .out8(ddrEnable), .out9(PORT_Enable),
    .out10(PIN_Enable), .out11(update), .out12(prescaler2), .out13(prescaler1), .out14(mask), .in(and_3_out),
    .sel(bit_extender_5_out));  // open: out15
  or or_2 (PCEnable, and_1_out, and_2_out, demultiplexer_1_out7);
  Comparator #(.mode("unsigned"), .width(2)) comparator_6 (
    .a(operand1_t), .b(2'b01), .gt(comparator_6_gt));  // open: eq, lt
  Comparator #(.mode("unsigned"), .width(2)) comparator_7 (
    .a(operand2_t), .b(2'b00), .gt(comparator_7_gt));  // open: eq, lt
  and and_4 (ramoutputEnable, comparator_6_gt, comparator_1_eq);
  Comparator #(.mode("unsigned"), .width(2)) comparator_8 (
    .a(operand1_t), .b(2'b01), .gt(comparator_8_gt));  // open: eq, lt
  and and_5 (ramWrtieEnable, comparator_7_gt, comparator_1_eq);
  assign ramInput = or_3_out ? ALUinput1 : 8'bz;  // Controlled_Buffer controlled_buffer_1
  or or_3 (or_3_out, ramoutputEnable, or_4_out);
  Multiplexer #(.width(8)) multiplexer_7 (.in0(ALUinput2), .in1(data1), .out(multiplexer_7_out), .sel(comparator_8_gt));
  or or_4 (or_4_out, ramoutputEnable, ramWrtieEnable);
  assign ramAdress = or_4_out ? multiplexer_7_out : 8'bz;  // Controlled_Buffer controlled_buffer_2

  assign ALU_select = insturction;
  assign regData = ALUinput1;

  // Other names for the same wires on the sheet: instr[7:0] = insturction

  // Notes on the sheet:
  //   Registers Enable pins
endmodule

module TRAM_CONTROLLER (
  input  pcEnable,
  input  [7:0] regData,
  input  [7:0] mask,
  input  maskEnable,
  input  c,
  input  [7:0] prescaler,
  input  prescEnable,
  output Enable,
  output [7:0] pcData,
  output out_10,
  output out_11,
  output [7:0] out_12,
  output [7:0] prescalerO
);

  wire and_1_out, bit_extender_1_out, comparator_1_eq, comparator_2_eq, comparator_3_eq, register_2_q,
       tram_1_out_5;
  wire [2:0] counter_1_q;
  wire [7:0] register_1_q, tram_1_out_4;

  Bit_Extender #(.out_width(1)) bit_extender_1 (.in(mask), .out(bit_extender_1_out));
  Register #(.width(1)) maskReg (.D(bit_extender_1_out), .en(maskEnable), .clk(c), .Q(out_10));  // open: clr
  Register prescalerReg (.D(prescaler), .en(prescEnable), .clk(c), .Q(prescalerO));  // open: clr
  Register register_1 (
    .D(tram_1_out_4), .en(tram_1_out_5), .clk(tram_1_out_5), .Q(register_1_q), .clr(comparator_1_eq));
  Multiplexer multiplexer_1 (.in0(pcEnable), .in1(1'b1), .out(Enable), .sel(and_1_out));
  Multiplexer #(.width(8)) multiplexer_2 (.in0(regData), .in1(register_1_q), .out(pcData), .sel(and_1_out));
  and and_1 (and_1_out, register_2_q, comparator_2_eq);
  Register #(.width(1)) register_2 (
    .D(tram_1_out_5), .en(tram_1_out_5), .clk(tram_1_out_5), .Q(register_2_q), .clr(comparator_1_eq));
  Tram tram_1 (
    .out_5(tram_1_out_5), .out_6(out_12), .out_4(tram_1_out_4), .mask(out_10), .c(c), .prescaler(prescalerO));  // open: out_7
  Counter #(.max('h7), .width(3)) counter_1 (
    .count(register_2_q), .Q(counter_1_q), .clk(c), .clr(comparator_1_eq));  // open: load, D, carry, up
  Comparator #(.mode("unsigned"), .width(3)) comparator_1 (
    .a(3'b011), .b(counter_1_q), .eq(comparator_1_eq));  // open: gt, lt
  Comparator #(.mode("unsigned"), .width(3)) comparator_2 (
    .a(3'b010), .b(counter_1_q), .eq(comparator_2_eq));  // open: gt, lt
  Comparator #(.mode("unsigned"), .width(3)) comparator_3 (
    .a(counter_1_q), .b(3'b000), .eq(comparator_3_eq));  // open: gt, lt
  and and_2 (out_11, comparator_3_eq, register_2_q);
endmodule

module PORT_CONTROLLER (
  input  clk,
  input  UpdateEnable,
  input  [7:0] RegData,
  input  DDREnable,
  input  portEnable,
  input  PrescalerEnable,
  input  InputEnable,
  output [7:0] out_8,
  output [7:0] out_9,
  output [7:0] Ooutput,
  output [7:0] out_11,
  output [7:0] out_12,
  output [7:0] Counter,
  output [7:0] out_14
);

  wire bit_extender_1_out, prescaler_counter_1_out_3, UpdateReg_q;

  Register DdrReg (.D(RegData), .en(DDREnable), .clk(clk), .Q(out_8));  // open: clr
  Register PrescalerReg (.D(RegData), .en(PrescalerEnable), .clk(clk), .Q(out_14));  // open: clr
  Register PortReg (.D(RegData), .en(portEnable), .clk(clk), .Q(out_9));  // open: clr
  Prescaler_Counter prescaler_counter_1 (
    .out_3(prescaler_counter_1_out_3), .counter(Counter), .clk(clk), .prescaler(out_14));
  Register #(.width(1)) UpdateReg (.D(bit_extender_1_out), .en(UpdateEnable), .clk(clk), .Q(UpdateReg_q));  // open: clr
  Bit_Extender #(.out_width(1)) bit_extender_1 (.in(RegData), .out(bit_extender_1_out));
  port_helper port_helper_1 (
    .PIin(out_11), .Ooutput(Ooutput), .in_4(prescaler_counter_1_out_3), .DDR(out_8), .PpORT(out_9),
    .UPDATE(UpdateReg_q), .Iinput(out_12));
  Register InputReg (.D(RegData), .en(InputEnable), .clk(clk), .Q(out_12));  // open: clr
endmodule

module my_counter (
  input  [7:0] prescaler,
  input  clock,
  output reset,
  output [7:0] counter
);

  wire and_1_out, and_2_out, j_k_ff_1_qn, j_k_ff_2_qn, j_k_ff_3_qn, j_k_ff_4_qn, j_k_ff_5_qn, j_k_ff_6_qn,
       j_k_ff_7_qn, j_k_ff_8_qn, not_1_out, not_2_out, not_3_out, not_4_out, not_5_out, not_6_out, not_7_out,
       not_8_out, not_9_out, not_10_out, not_11_out, not_12_out, not_13_out, not_14_out, not_15_out,
       not_16_out, or_1_out, xnor_1_out, xnor_2_out, xnor_3_out, xnor_4_out, xnor_5_out, xnor_6_out,
       xnor_7_out, xnor_8_out;

  or or_1 (or_1_out, prescaler[0], prescaler[1], prescaler[2], prescaler[3], prescaler[4], prescaler[5], prescaler[6], prescaler[7]);
  J_K_Flip_Flop j_k_ff_1 (
    .J(j_k_ff_1_qn), .K(not_1_out), .clk(clock), .Q(counter[0]), .Qn(j_k_ff_1_qn), .reset(and_2_out));  // open: preset
  not not_1 (not_1_out, j_k_ff_1_qn);
  not not_2 (not_2_out, j_k_ff_2_qn);
  J_K_Flip_Flop j_k_ff_2 (
    .J(j_k_ff_2_qn), .K(not_2_out), .clk(j_k_ff_1_qn), .Q(counter[1]), .Qn(j_k_ff_2_qn), .reset(and_2_out));  // open: preset
  J_K_Flip_Flop j_k_ff_3 (
    .J(j_k_ff_3_qn), .K(not_3_out), .clk(j_k_ff_2_qn), .Q(counter[2]), .Qn(j_k_ff_3_qn), .reset(and_2_out));  // open: preset
  not not_3 (not_3_out, j_k_ff_3_qn);
  J_K_Flip_Flop j_k_ff_4 (
    .J(j_k_ff_4_qn), .K(not_4_out), .clk(j_k_ff_3_qn), .Q(counter[3]), .Qn(j_k_ff_4_qn), .reset(and_2_out));  // open: preset
  not not_4 (not_4_out, j_k_ff_4_qn);
  J_K_Flip_Flop j_k_ff_5 (
    .J(j_k_ff_5_qn), .K(not_5_out), .clk(j_k_ff_4_qn), .Q(counter[4]), .Qn(j_k_ff_5_qn), .reset(and_2_out));  // open: preset
  not not_5 (not_5_out, j_k_ff_5_qn);
  xnor xnor_1 (xnor_1_out, prescaler[0], counter[0]);
  xnor xnor_2 (xnor_2_out, prescaler[1], counter[1]);
  xnor xnor_3 (xnor_3_out, prescaler[2], counter[2]);
  xnor xnor_4 (xnor_4_out, prescaler[3], counter[3]);
  xnor xnor_5 (xnor_5_out, prescaler[4], counter[4]);
  xnor xnor_6 (xnor_6_out, prescaler[5], counter[5]);
  xnor xnor_7 (xnor_7_out, prescaler[6], counter[6]);
  xnor xnor_8 (xnor_8_out, prescaler[7], counter[7]);
  J_K_Flip_Flop j_k_ff_6 (
    .J(j_k_ff_6_qn), .K(not_6_out), .clk(j_k_ff_5_qn), .Q(counter[5]), .Qn(j_k_ff_6_qn), .reset(and_2_out));  // open: preset
  not not_6 (not_6_out, j_k_ff_6_qn);
  and and_1 (and_1_out, xnor_1_out, xnor_2_out, xnor_3_out, xnor_4_out, xnor_5_out, xnor_6_out, xnor_7_out, xnor_8_out);
  J_K_Flip_Flop j_k_ff_7 (
    .J(j_k_ff_7_qn), .K(not_7_out), .clk(j_k_ff_6_qn), .Q(counter[6]), .Qn(j_k_ff_7_qn), .reset(and_2_out));  // open: preset
  not not_7 (not_7_out, j_k_ff_7_qn);
  J_K_Flip_Flop j_k_ff_8 (
    .J(j_k_ff_8_qn), .K(not_8_out), .clk(j_k_ff_7_qn), .Q(counter[7]), .Qn(j_k_ff_8_qn), .reset(and_2_out));  // open: preset
  not not_8 (not_8_out, j_k_ff_8_qn);
  not not_9 (not_9_out, not_10_out);
  and and_2 (and_2_out, not_9_out, 1'b1);
  not not_10 (not_10_out, not_11_out);
  not not_11 (not_11_out, not_12_out);
  not not_12 (not_12_out, not_13_out);
  and and_3 (reset, and_1_out, or_1_out);
  not not_13 (not_13_out, not_14_out);
  not not_14 (not_14_out, not_15_out);
  not not_15 (not_15_out, not_16_out);
  not not_16 (not_16_out, and_1_out);
endmodule

module romCounter (
  input  setE,
  input  [7:0] setAddr,
  input  clock,
  input  [7:0] precaler,
  output [7:0] romAdress
);

  wire and_1_out, comparator_1_eq, or_1_out;
  wire [7:0] counter_1_q;

  Counter counter_1 (.Q(counter_1_q), .clk(clock), .clr(comparator_1_eq));  // open: load, D, count, carry, up
  Comparator comparator_1 (.a(counter_1_q), .b(precaler), .eq(comparator_1_eq));  // open: gt, lt
  Counter counter_2 (.load(setE), .D(setAddr), .Q(romAdress), .clk(or_1_out));  // open: count, carry, up, clr
  or or_1 (or_1_out, comparator_1_eq, and_1_out);
  and and_1 (and_1_out, clock, setE);
endmodule

module myDecoder (
  input  [31:0] command,
  output [7:0] instruction,
  output [3:0] operand1,
  output [7:0] data1,
  output [3:0] operand2,
  output [7:0] data2
);


  assign data1 = command[19:12];
  assign data2 = command[7:0];
  assign instruction = command[31:24];
  assign operand1 = command[23:20];
  assign operand2 = command[11:8];
endmodule

module PCcontrol (
  input  c,
  input  [7:0] presc,
  input  pcE,
  input  [7:0] pcI,
  input  in_5,
  output [7:0] romAdress
);

  wire and_1_out, and_2_out, not_1_out, not_2_out, not_3_out, not_4_out, not_5_out, not_6_out, not_7_out;
  wire [7:0] multiplexer_1_out, romcounter_1_romadress;

  and and_1 (and_1_out, not_1_out, 1'b1);
  not not_1 (not_1_out, not_2_out);
  not not_2 (not_2_out, not_3_out);
  not not_3 (not_3_out, not_4_out);
  not not_4 (not_4_out, not_5_out);
  not not_5 (not_5_out, not_6_out);
  not not_6 (not_6_out, not_7_out);
  not not_7 (not_7_out, in_5);
  and and_2 (and_2_out, c, and_1_out);
  romCounter romcounter_1 (
    .romAdress(romcounter_1_romadress), .clock(and_2_out), .precaler(presc), .setAddr(pcI), .setE(pcE));
  Register PC (.D(multiplexer_1_out), .en(1'b1), .clk(and_2_out), .Q(romAdress));  // open: clr
  Multiplexer #(.width(8)) multiplexer_1 (.in0(romcounter_1_romadress), .in1(pcI), .out(multiplexer_1_out), .sel(pcE));
endmodule

module Tram (
  input  mask,
  input  [7:0] prescaler,
  input  c,
  output [7:0] out_4,
  output out_5,
  output [7:0] out_6,
  output out_7
);

  wire and_1_out, comparator_1_gt, my_counter_1_reset, my_counter_2_reset, not_1_out, not_2_out, not_3_out,
       not_4_out, not_5_out, not_6_out, not_7_out, not_8_out;

  my_counter my_counter_1 (.prescaler(prescaler), .clock(c), .reset(my_counter_1_reset));  // open: counter
  my_counter my_counter_2 (
    .prescaler({8{1'b1}}), .clock(my_counter_1_reset), .reset(my_counter_2_reset), .counter(out_6));
  and and_1 (and_1_out, mask, my_counter_2_reset);
  not not_1 (not_1_out, and_1_out);
  Comparator #(.mode("unsigned")) comparator_1 (.a(out_6), .b(8'hfd), .gt(comparator_1_gt));  // open: eq, lt
  assign out_4 = and_1_out ? 8'h1 : 8'bz;  // Controlled_Buffer controlled_buffer_1
  not not_2 (not_2_out, and_1_out);
  and and_2 (out_7, not_1_out, comparator_1_gt);
  not not_3 (not_3_out, not_4_out);
  not not_4 (not_4_out, not_2_out);
  not not_5 (not_5_out, not_3_out);
  not not_6 (not_6_out, not_5_out);
  not not_7 (not_7_out, not_6_out);
  not not_8 (not_8_out, not_7_out);
  not not_9 (out_5, not_8_out);
endmodule

module Prescaler_Counter (
  input  [7:0] prescaler,
  input  clk,
  output out_3,
  output [7:0] counter
);

  wire my_counter_1_reset;

  my_counter my_counter_1 (.prescaler(prescaler), .clock(clk), .reset(my_counter_1_reset));  // open: counter
  my_counter my_counter_2 (.prescaler({8{1'b1}}), .clock(my_counter_1_reset), .reset(out_3), .counter(counter));
endmodule

module port_helper (
  input  UPDATE,
  input  [7:0] DDR,
  input  [7:0] PpORT,
  input  in_4,
  input  [7:0] Iinput,
  output [7:0] Ooutput,
  output [7:0] PIin
);

  wire and_1_out, not_2_out, not_3_out, not_4_out, not_5_out, or_2_out;
  wire [7:0] multiplexer_1_out, not_1_out, register_1_q;

  assign not_1_out = ~register_1_q;  // NOT_Gate not_1, 8 bits wide
  Multiplexer #(.width(8)) multiplexer_1 (.in0(PpORT), .in1(not_1_out), .out(multiplexer_1_out), .sel(in_4));
  not not_2 (not_2_out, in_4);
  not not_3 (not_3_out, not_2_out);
  assign PIin = register_1_q | Iinput;  // OR_Gate or_1, 8 bits wide
  or or_2 (or_2_out, UPDATE, and_1_out);
  and and_1 (and_1_out, 1'b1, not_5_out);
  not not_4 (not_4_out, not_3_out);
  not not_5 (not_5_out, not_4_out);
  Register register_1 (.D(multiplexer_1_out), .Q(register_1_q), .clk(or_2_out));  // open: en, clr
  assign Ooutput = DDR & register_1_q;  // AND_Gate and_2, 8 bits wide
endmodule
